// Logisim project processador.circ as structural Verilog: 13 circuits, main circuit processor
module Example (
);

  wire button_1_out, button_2_out, processor_1_clk_ram, processor_1_we_ram_learning, processor_1_we_ram_write;
  wire [7:0] processor_1_data_ram_out, processor_1_memory_ram_out, processor_1_memory_rom_out, ram_1_dout;
  wire [15:0] rom_1_data;

  Button button_1 (.out(button_1_out));
  Button button_2 (.out(button_2_out));
  ROM #(.dataWidth(16)) rom_1 (.addr(processor_1_memory_rom_out), .data(rom_1_data));
  processor processor_1 (
    .CLK_general(button_1_out), .RESET_PC(button_2_out), .DATA_ROM_in(rom_1_data), .DATA_RAM_in(ram_1_dout),
    .Memory_ROM_out(processor_1_memory_rom_out), .Memory_RAM_out(processor_1_memory_ram_out),
    .WE_RAM_learning(processor_1_we_ram_learning), .WE_RAM_Write(processor_1_we_ram_write),
    .CLK_RAM(processor_1_clk_ram), .DATA_RAM_out(processor_1_data_ram_out));
  RAM ram_1 (
    .addr(processor_1_memory_ram_out), .we(processor_1_we_ram_learning), .oe(processor_1_we_ram_write),
    .clk(processor_1_clk_ram), .din(processor_1_data_ram_out), .dout(ram_1_dout));
endmodule

module processor (
  input  CLK_general,
  input  RESET_PC,
  input  [15:0] DATA_ROM_in,
  input  [7:0] DATA_RAM_in,
  output [7:0] Memory_ROM_out,
  output [7:0] Memory_RAM_out,
  output WE_RAM_learning,
  output WE_RAM_Write,
  output CLK_RAM,
  output [7:0] DATA_RAM_out
);

  wire cu_1_freeze_pc, cu_1_halt, cu_1_reset_clock, cu_1_slc_jmp_pc, cu_1_we, cycle_counter_1_data_clock,
       cycle_counter_1_ir_clock, cycle_counter_1_pc_clock, ula_1_carry, ula_1_nd, ula_1_zr;
  wire [2:0] cu_1_opcode_ula_out, cu_1_slc_data_out, cu_1_slca_data_out, cu_1_slcb_data_out;
  wire [7:0] cu_1_jpm_pc, cu_1_response_data, registradores_data_1_b_out, ula_1_not_r, ula_1_r;
  wire [15:0] ir_1_ir_out;

  IR ir_1 (.DATA_ROM_in(DATA_ROM_in), .IR_write(cycle_counter_1_ir_clock), .IR_out(ir_1_ir_out));
  Cycle_counter cycle_counter_1 (
    .CLK(CLK_general), .HALT(cu_1_halt), .Reset(cu_1_reset_clock), .PC_clock(cycle_counter_1_pc_clock),
    .IR_clock(cycle_counter_1_ir_clock), .RAM_clock(CLK_RAM), .DATA_clock(cycle_counter_1_data_clock));
  CU cu_1 (
    .Comand_in(ir_1_ir_out), .Response_ULA(ula_1_r), .NOT_RESPONSE_ULA(ula_1_not_r), .ND_ULA(ula_1_nd),
    .ZR_ULA(ula_1_zr), .CARRY_ULA(ula_1_carry), .RAM_in(DATA_RAM_in), .ResponseA_DATA(DATA_RAM_out),
    .RESET_clock(cu_1_reset_clock), .JPM_PC(cu_1_jpm_pc), .SLC_JMP_PC(cu_1_slc_jmp_pc),
    .FREEZE_PC(cu_1_freeze_pc), .WE(cu_1_we), .SLC_DATA_out(cu_1_slc_data_out),
    .RESPONSE_DATA(cu_1_response_data), .SLCA_DATA_out(cu_1_slca_data_out),
    .SLCB_DATA_out(cu_1_slcb_data_out), .OpCode_ULA_out(cu_1_opcode_ula_out),
    .Local_memory_RAM(Memory_RAM_out), .WE_RAM_Learning(WE_RAM_learning), .WE_RAM_out(WE_RAM_Write),
    .HALT(cu_1_halt));
  PC pc_1 (
    .JMP_in(cu_1_jpm_pc), .SLC_JMP(cu_1_slc_jmp_pc), .Freeze(cu_1_freeze_pc), .CLK(cycle_counter_1_pc_clock),
    .RESET(RESET_PC), .R_out(Memory_ROM_out));
  Registradores_DATA registradores_data_1 (
    .CLK(cycle_counter_1_data_clock), .WE(cu_1_we), .SLC_in(cu_1_slc_data_out), .DATA_in(cu_1_response_data),
    .SLCA_out(cu_1_slca_data_out), .SLCB_out(cu_1_slcb_data_out), .A_out(DATA_RAM_out),
    .B_out(registradores_data_1_b_out));
  ULA ula_1 (
    .A(DATA_RAM_out), .B(registradores_data_1_b_out), .OpCode(cu_1_opcode_ula_out), .R(ula_1_r),
    .NOT_R(ula_1_not_r), .ND(ula_1_nd), .ZR(ula_1_zr), .CARRY(ula_1_carry));
endmodule

module PC (
  input  [7:0] JMP_in,
  input  SLC_JMP,
  input  Freeze,
  input  CLK,
  input  RESET,
  output [7:0] R_out
);

  wire not_1_out;
  wire [7:0] adder_1_out, multiplexer_1_out;

  Register Register_PC (.D(multiplexer_1_out), .en(not_1_out), .clk(CLK), .Q(R_out), .clr(RESET));
  Multiplexer #(.width(8)) multiplexer_1 (.in0(adder_1_out), .in1(JMP_in), .out(multiplexer_1_out), .sel(SLC_JMP));
  not not_1 (not_1_out, Freeze);
  Adder adder_1 (.a(R_out), .b(8'h1), .out(adder_1_out));  // open: cin, cout
endmodule

module IR (
  input  [15:0] DATA_ROM_in,
  input  IR_write,
  output [15:0] IR_out
);

  Register #(.width(16)) register_1 (.D(DATA_ROM_in), .en(IR_write), .clk(IR_write), .Q(IR_out));  // open: clr
endmodule

module Cycle_counter (
  input  CLK,
  input  HALT,
  input  Reset,
  output PC_clock,
  output IR_clock,
  output RAM_clock,
  output DATA_clock
);

  wire not_1_out;
  wire [1:0] adder_1_out, Conte_CLOCK_q;

  Adder #(.width(2)) adder_1 (.a(Conte_CLOCK_q), .b(2'b01), .out(adder_1_out));  // open: cin, cout
  Register #(.width(2)) Conte_CLOCK (.D(adder_1_out), .en(not_1_out), .clk(CLK), .Q(Conte_CLOCK_q), .clr(Reset));
  not not_1 (not_1_out, HALT);
  Demultiplexer #(.select(2)) demultiplexer_1 (
    .out0(PC_clock), .out1(IR_clock), .out2(RAM_clock), .out3(DATA_clock), .in(1'b1), .sel(Conte_CLOCK_q));
endmodule

module Registradores_DATA (
  input  CLK,
  input  WE,
  input  [2:0] SLC_in,
  input  [7:0] DATA_in,
  input  [2:0] SLCA_out,
  input  [2:0] SLCB_out,
  output [7:0] A_out,
  output [7:0] B_out
);

  wire demultiplexer_1_out0, demultiplexer_1_out1, demultiplexer_1_out2, demultiplexer_1_out3,
       demultiplexer_1_out4, demultiplexer_1_out5, demultiplexer_1_out6, demultiplexer_1_out7;
  wire [7:0] B0_q, B1_q, B2_q, B3_q, demultiplexer_2_out0, demultiplexer_2_out1, demultiplexer_2_out2,
       demultiplexer_2_out3, demultiplexer_2_out4, demultiplexer_2_out5, demultiplexer_2_out6,
       demultiplexer_2_out7, T0_q, T1_q, T2_q, T3_q;

  Demultiplexer #(.select(3)) demultiplexer_1 (
    .out0(demultiplexer_1_out0), .out1(demultiplexer_1_out1), .out2(demultiplexer_1_out2),
    .out3(demultiplexer_1_out3), .out4(demultiplexer_1_out4), .out5(demultiplexer_1_out5),
    .out6(demultiplexer_1_out6), .out7(demultiplexer_1_out7), .in(WE), .sel(SLC_in));
  Demultiplexer #(.select(3), .width(8)) demultiplexer_2 (
    .out0(demultiplexer_2_out0), .out1(demultiplexer_2_out1), .out2(demultiplexer_2_out2),
    .out3(demultiplexer_2_out3), .out4(demultiplexer_2_out4), .out5(demultiplexer_2_out5),
    .out6(demultiplexer_2_out6), .out7(demultiplexer_2_out7), .in(DATA_in), .sel(SLC_in));
  Register B0 (.D(demultiplexer_2_out0), .en(demultiplexer_1_out0), .clk(CLK), .Q(B0_q));  // open: clr
  Register B3 (.D(demultiplexer_2_out3), .en(demultiplexer_1_out3), .clk(CLK), .Q(B3_q));  // open: clr
  Register T0 (.D(demultiplexer_2_out4), .en(demultiplexer_1_out4), .clk(CLK), .Q(T0_q));  // open: clr
  Register T3 (.D(demultiplexer_2_out7), .en(demultiplexer_1_out7), .clk(CLK), .Q(T3_q));  // open: clr
  Register B1 (.D(demultiplexer_2_out1), .en(demultiplexer_1_out1), .clk(CLK), .Q(B1_q));  // open: clr
  Register B2 (.D(demultiplexer_2_out2), .en(demultiplexer_1_out2), .clk(CLK), .Q(B2_q));  // open: clr
  Register T1 (.D(demultiplexer_2_out5), .en(demultiplexer_1_out5), .clk(CLK), .Q(T1_q));  // open: clr
  Register T2 (.D(demultiplexer_2_out6), .en(demultiplexer_1_out6), .clk(CLK), .Q(T2_q));  // open: clr
  Multiplexer #(.select(3), .width(8)) multiplexer_1 (
    .in0(B0_q), .in1(B1_q), .in2(B2_q), .in3(B3_q), .in4(T0_q), .in5(T1_q), .in6(T2_q), .in7(T3_q),
    .out(B_out), .sel(SLCB_out));
  Multiplexer #(.select(3), .width(8)) multiplexer_2 (
    .in0(B0_q), .in1(B1_q), .in2(B2_q), .in3(B3_q), .in4(T0_q), .in5(T1_q), .in6(T2_q), .in7(T3_q),
    .out(A_out), .sel(SLCA_out));
endmodule

module ULA (
  input  [7:0] A,
  input  [7:0] B,
  input  [2:0] OpCode,
  output [7:0] R,
  output [7:0] NOT_R,
  output ND,
  output ZR,
  output CARRY
);

  wire adder_1_cout, bit_extender_1_out, bit_extender_2_out, subtractor_1_bout;
  wire [7:0] adder_1_out, and_1_out, divider_1_out, divider_1_rem, multiplier_1_cout, multiplier_1_out,
       not_1_out, or_1_out, subtractor_1_out, xor_1_out;

  Multiplier multiplier_1 (.a(A), .b(8'h2), .out(multiplier_1_out), .cout(multiplier_1_cout));  // open: cin
  Divider divider_1 (.a(A), .b(8'h2), .out(divider_1_out), .rem(divider_1_rem));  // open: upper
  assign not_1_out = ~A;  // NOT_Gate not_1, 8 bits wide
  Adder adder_1 (.a(A), .b(B), .out(adder_1_out), .cout(adder_1_cout));  // open: cin
  Subtractor subtractor_1 (.a(A), .b(B), .out(subtractor_1_out), .bout(subtractor_1_bout));  // open: bin
  assign and_1_out = A & B;  // AND_Gate and_1, 8 bits wide
  assign or_1_out = A | B;  // OR_Gate or_1, 8 bits wide
  assign xor_1_out = A ^ B;  // XOR_Gate xor_1, 8 bits wide
  Bit_Extender #(.out_width(1)) bit_extender_1 (.in(divider_1_rem), .out(bit_extender_1_out));
  Multiplexer #(.select(3), .width(8)) multiplexer_1 (
    .in0(multiplier_1_out), .in1(divider_1_out), .in2(not_1_out), .in3(adder_1_out), .in4(subtractor_1_out),
    .in5(and_1_out), .in6(or_1_out), .in7(xor_1_out), .out(R), .sel(OpCode));
  Bit_Extender #(.out_width(1)) bit_extender_2 (.in(multiplier_1_cout), .out(bit_extender_2_out));
  Multiplexer #(.select(3)) multiplexer_2 (
    .in0(bit_extender_2_out), .in1(bit_extender_1_out), .in2(1'b0), .in3(adder_1_cout),
    .in4(subtractor_1_bout), .in5(1'b0), .in6(1'b0), .in7(1'b0), .out(CARRY), .sel(OpCode));
  assign NOT_R = ~R;  // NOT_Gate not_2, 8 bits wide
  BitSelector bitselector_1 (.in(R), .out(ND), .sel(3'b111));
  Comparator #(.mode("unsigned")) comparator_1 (.a(R), .b({8{1'b0}}), .eq(ZR));  // open: gt, lt
endmodule

module CU (
  input  [15:0] Comand_in,
  input  [7:0] Response_ULA,
  input  [7:0] NOT_RESPONSE_ULA,
  input  ND_ULA,
  input  ZR_ULA,
  input  CARRY_ULA,
  input  [7:0] RAM_in,
  input  [7:0] ResponseA_DATA,
  output RESET_clock,
  output [7:0] JPM_PC,
  output SLC_JMP_PC,
  output FREEZE_PC,
  output WE,
  output [2:0] SLC_DATA_out,
  output [7:0] RESPONSE_DATA,
  output [2:0] SLCA_DATA_out,
  output [2:0] SLCB_DATA_out,
  output [2:0] OpCode_ULA_out,
  output [7:0] Local_memory_RAM,
  output WE_RAM_Learning,
  output WE_RAM_out,
  output HALT
);

  wire decoder_1_out0, decoder_1_out1, decoder_1_out2, decoder_1_out3, decoder_1_out4, decoder_1_out5,
       decoder_1_out6, or_1_out, or_2_out;

  Decoder #(.enable("false"), .select(3)) decoder_1 (
    .out0(decoder_1_out0), .out1(decoder_1_out1), .out2(decoder_1_out2), .out3(decoder_1_out3),
    .out4(decoder_1_out4), .out5(decoder_1_out5), .out6(decoder_1_out6), .out7(HALT), .sel(Comand_in[15:13]));
  or or_1 (or_1_out, decoder_1_out0, decoder_1_out1, decoder_1_out2, decoder_1_out3);
  or or_2 (or_2_out, decoder_1_out4, decoder_1_out5);
  BASIC_Operation basic_operation_1 (
    .BIN_in(Comand_in), .ULA_in(Response_ULA), .NOT_ULA_in(NOT_RESPONSE_ULA), .ND_ULA(ND_ULA),
    .ZR_ULA(ZR_ULA), .CARRY_ULA(CARRY_ULA), .Active(or_1_out), .DONT_RESETE_clock(RESET_clock),
    .JPM_PC(JPM_PC), .SLC_JMP_PC(SLC_JMP_PC), .FREEZE_PC(FREEZE_PC), .WE(WE), .SLC_DATA_out(SLC_DATA_out),
    .RESPONSE_DATA(RESPONSE_DATA), .SLCA_DATA_out(SLCA_DATA_out), .SLCB_DATA_out(SLCB_DATA_out),
    .OpCode_ULA_out(OpCode_ULA_out), .Local_memory_RAM(Local_memory_RAM), .WE_RAM_Learning(WE_RAM_Learning),
    .WE_RAM_out(WE_RAM_out), .HALT(HALT));
  RAM_Controler ram_controler_1 (
    .BIN_in(Comand_in), .RAM_in(RAM_in), .Active(or_2_out), .DONT_RESETE_clock(RESET_clock), .JPM_PC(JPM_PC),
    .SLC_JMP_PC(SLC_JMP_PC), .FREEZE_PC(FREEZE_PC), .WE(WE), .SLC_DATA_out(SLC_DATA_out),
    .RESPONSE_DATA(RESPONSE_DATA), .SLCA_DATA_out(SLCA_DATA_out), .SLCB_DATA_out(SLCB_DATA_out),
    .OpCode_ULA_out(OpCode_ULA_out), .Local_memory_RAM(Local_memory_RAM), .WE_RAM_Learning(WE_RAM_Learning),
    .WE_RAM_out(WE_RAM_out), .HALT(HALT));
  JUMP_Controler jump_controler_1 (
    .BIN_in(Comand_in), .ResponseA_DATA(ResponseA_DATA), .Active(decoder_1_out6),
    .DONT_RESETE_clock(RESET_clock), .JPM_PC(JPM_PC), .SLC_JMP_PC(SLC_JMP_PC), .FREEZE_PC(FREEZE_PC),
    .WE(WE), .SLC_DATA_out(SLC_DATA_out), .RESPONSE_DATA(RESPONSE_DATA), .SLCA_DATA_out(SLCA_DATA_out),
    .SLCB_DATA_out(SLCB_DATA_out), .OpCode_ULA_out(OpCode_ULA_out), .Local_memory_RAM(Local_memory_RAM),
    .WE_RAM_Learning(WE_RAM_Learning), .WE_RAM_out(WE_RAM_out), .HALT(HALT));

  // Notes on the sheet:
  //   :add
  //   :sub
  //   :AND
  //   :OR
  //   toSave
  //   toSave
  //   toSave
  //   toSave
  //   varA
  //   varA
  //   varA
  //   varA
  //   varB
  //   varB
  //   varB
  //   varB
  //   save
  //   save
  //   save
  //   save
  //   aritmetic
  //   aritmetic
  //   aritmetic
  //   aritmetic
  //   |
  //   :LOAD
  //   :STORE
  //   :JUMP
  //   |
  //   :HALT
  //   toSave
  //   VAR_A
  //   not
  //   GetValue
  //   RAM
  //   not
  //   RAM
  //   conditional
  //   ROM
endmodule

module RAM_Controler (
  input  [15:0] BIN_in,
  input  [7:0] RAM_in,
  input  Active,
  output DONT_RESETE_clock,
  output [7:0] JPM_PC,
  output SLC_JMP_PC,
  output FREEZE_PC,
  output WE,
  output [2:0] SLC_DATA_out,
  output [7:0] RESPONSE_DATA,
  output [2:0] SLCA_DATA_out,
  output [2:0] SLCB_DATA_out,
  output [2:0] OpCode_ULA_out,
  output [7:0] Local_memory_RAM,
  output WE_RAM_Learning,
  output WE_RAM_out,
  output HALT
);

  wire [7:0] multiplexer_1_out, not_1_out;

  assign not_1_out = ~RAM_in;  // NOT_Gate not_1, 8 bits wide
  Multiplexer #(.width(8)) multiplexer_1 (.in0(RAM_in), .in1(not_1_out), .out(multiplexer_1_out), .sel(BIN_in[9]));
  assign DONT_RESETE_clock = Active ? ~1'b1 : 1'bz;  // Controlled_Inverter controlled_inverter_1
  assign JPM_PC = Active ? {8{1'b0}} : 8'bz;  // Controlled_Buffer controlled_buffer_1
  assign SLC_JMP_PC = Active ? 1'b0 : 1'bz;  // Controlled_Buffer controlled_buffer_2
  assign FREEZE_PC = Active ? 1'b0 : 1'bz;  // Controlled_Buffer controlled_buffer_3
  assign WE = Active ? ~BIN_in[13] : 1'bz;  // Controlled_Inverter controlled_inverter_2
  assign SLC_DATA_out = Active ? BIN_in[12:10] : 3'bz;  // Controlled_Buffer controlled_buffer_4
  assign RESPONSE_DATA = Active ? multiplexer_1_out : 8'bz;  // Controlled_Buffer controlled_buffer_5
  assign SLCA_DATA_out = Active ? BIN_in[12:10] : 3'bz;  // Controlled_Buffer controlled_buffer_6
  assign SLCB_DATA_out = Active ? 3'b000 : 3'bz;  // Controlled_Buffer controlled_buffer_7
  assign OpCode_ULA_out = Active ? 3'b000 : 3'bz;  // Controlled_Buffer controlled_buffer_8
  assign Local_memory_RAM = Active ? BIN_in[7:0] : 8'bz;  // Controlled_Buffer controlled_buffer_9
  assign WE_RAM_Learning = Active ? BIN_in[13] : 1'bz;  // Controlled_Buffer controlled_buffer_10
  assign WE_RAM_out = Active ? ~BIN_in[13] : 1'bz;  // Controlled_Inverter controlled_inverter_3
  assign HALT = Active ? ~1'b1 : 1'bz;  // Controlled_Inverter controlled_inverter_4
endmodule

module JUMP_Controler (
  input  [15:0] BIN_in,
  input  [7:0] ResponseA_DATA,
  input  Active,
  output DONT_RESETE_clock,
  output [7:0] JPM_PC,
  output SLC_JMP_PC,
  output FREEZE_PC,
  output WE,
  output [2:0] SLC_DATA_out,
  output [7:0] RESPONSE_DATA,
  output [2:0] SLCA_DATA_out,
  output [2:0] SLCB_DATA_out,
  output [2:0] OpCode_ULA_out,
  output [7:0] Local_memory_RAM,
  output WE_RAM_Learning,
  output WE_RAM_out,
  output HALT
);

  wire and_1_out, and_2_out, comparator_1_eq, not_1_out, or_1_out;
  wire [7:0] bitselector_1_out, or_2_out;

  Comparator #(.mode("unsigned")) comparator_1 (
    .a(ResponseA_DATA), .b({8{1'b0}}), .eq(comparator_1_eq));  // open: gt, lt
  BitSelector #(.group(8), .width(16)) bitselector_1 (.in(BIN_in), .out(bitselector_1_out), .sel(1'b0));
  not not_1 (not_1_out, BIN_in[9]);
  and and_1 (and_1_out, not_1_out, 1'b1);
  and and_2 (and_2_out, BIN_in[9], comparator_1_eq);
  or or_1 (or_1_out, and_1_out, and_2_out);
  assign or_2_out = {8{1'b0}} | bitselector_1_out;  // OR_Gate or_2, 8 bits wide
  assign DONT_RESETE_clock = Active ? ~1'b1 : 1'bz;  // Controlled_Inverter controlled_inverter_1
  assign JPM_PC = Active ? or_2_out : 8'bz;  // Controlled_Buffer controlled_buffer_1
  assign SLC_JMP_PC = Active ? or_1_out : 1'bz;  // Controlled_Buffer controlled_buffer_2
  assign FREEZE_PC = Active ? 1'b0 : 1'bz;  // Controlled_Buffer controlled_buffer_3
  assign WE = Active ? 1'b0 : 1'bz;  // Controlled_Buffer controlled_buffer_4
  assign SLC_DATA_out = Active ? 3'b000 : 3'bz;  // Controlled_Buffer controlled_buffer_5
  assign RESPONSE_DATA = Active ? {8{1'b0}} : 8'bz;  // Controlled_Buffer controlled_buffer_6
  assign SLCA_DATA_out = Active ? BIN_in[12:10] : 3'bz;  // Controlled_Buffer controlled_buffer_7
  assign SLCB_DATA_out = Active ? 3'b000 : 3'bz;  // Controlled_Buffer controlled_buffer_8
  assign OpCode_ULA_out = Active ? 3'b000 : 3'bz;  // Controlled_Buffer controlled_buffer_9
  assign Local_memory_RAM = Active ? {8{1'b0}} : 8'bz;  // Controlled_Buffer controlled_buffer_10
  assign WE_RAM_Learning = Active ? 1'b0 : 1'bz;  // Controlled_Buffer controlled_buffer_11
  assign WE_RAM_out = Active ? 1'b0 : 1'bz;  // Controlled_Buffer controlled_buffer_12
  assign HALT = Active ? ~1'b1 : 1'bz;  // Controlled_Inverter controlled_inverter_2
endmodule

module BASIC_Operation (
  input  [15:0] BIN_in,
  input  [7:0] ULA_in,
  input  [7:0] NOT_ULA_in,
  input  ND_ULA,
  input  ZR_ULA,
  input  CARRY_ULA,
  input  Active,
  output DONT_RESETE_clock,
  output [7:0] JPM_PC,
  output SLC_JMP_PC,
  output FREEZE_PC,
  output WE,
  output [2:0] SLC_DATA_out,
  output [7:0] RESPONSE_DATA,
  output [2:0] SLCA_DATA_out,
  output [2:0] SLCB_DATA_out,
  output [2:0] OpCode_ULA_out,
  output [7:0] Local_memory_RAM,
  output WE_RAM_Learning,
  output WE_RAM_out,
  output HALT
);

  wire [2:0] decodofication_1_bin_out;
  wire [7:0] slc_response_ula_1_response_selected;

  SLC_RESPONSE_ULA slc_response_ula_1 (
    .Select_response(BIN_in[2:0]), .ULA_in(ULA_in), .NOT_ULA_in(NOT_ULA_in), .ND_ULA(ND_ULA),
    .ZR_ULA(ZR_ULA), .CARRY_ULA(CARRY_ULA), .RESPONSE_SELECTED(slc_response_ula_1_response_selected));
  assign DONT_RESETE_clock = Active ? ~1'b1 : 1'bz;  // Controlled_Inverter controlled_inverter_1
  assign JPM_PC = Active ? {8{1'b0}} : 8'bz;  // Controlled_Buffer controlled_buffer_1
  assign SLC_JMP_PC = Active ? 1'b0 : 1'bz;  // Controlled_Buffer controlled_buffer_2
  assign FREEZE_PC = Active ? 1'b0 : 1'bz;  // Controlled_Buffer controlled_buffer_3
  assign WE = Active ? BIN_in[3] : 1'bz;  // Controlled_Buffer controlled_buffer_4
  assign SLC_DATA_out = Active ? BIN_in[12:10] : 3'bz;  // Controlled_Buffer controlled_buffer_5
  assign RESPONSE_DATA = Active ? slc_response_ula_1_response_selected : 8'bz;  // Controlled_Buffer controlled_buffer_6
  assign SLCA_DATA_out = Active ? BIN_in[9:7] : 3'bz;  // Controlled_Buffer controlled_buffer_7
  assign SLCB_DATA_out = Active ? BIN_in[6:4] : 3'bz;  // Controlled_Buffer controlled_buffer_8
  assign Local_memory_RAM = Active ? {8{1'b0}} : 8'bz;  // Controlled_Buffer controlled_buffer_9
  assign WE_RAM_Learning = Active ? 1'b0 : 1'bz;  // Controlled_Buffer controlled_buffer_10
  assign WE_RAM_out = Active ? 1'b0 : 1'bz;  // Controlled_Buffer controlled_buffer_11
  assign HALT = Active ? ~1'b1 : 1'bz;  // Controlled_Inverter controlled_inverter_2
  assign OpCode_ULA_out = Active ? decodofication_1_bin_out : 3'bz;  // Controlled_Buffer controlled_buffer_12
  Decodofication decodofication_1 (.BIN_in(BIN_in[15:13]), .BIN_out(decodofication_1_bin_out));
endmodule

module SLC_RESPONSE_ULA (
  input  [2:0] Select_response,
  input  [7:0] ULA_in,
  input  [7:0] NOT_ULA_in,
  input  ND_ULA,
  input  ZR_ULA,
  input  CARRY_ULA,
  output [7:0] RESPONSE_SELECTED
);

  wire [7:0] bit_extender_1_out, bit_extender_2_out, bit_extender_3_out;

  assign bit_extender_1_out = {{7{ND_ULA}}, ND_ULA};  // Bit_Extender bit_extender_1
  assign bit_extender_2_out = {{7{ZR_ULA}}, ZR_ULA};  // Bit_Extender bit_extender_2
  assign bit_extender_3_out = {{7{CARRY_ULA}}, CARRY_ULA};  // Bit_Extender bit_extender_3
  Multiplexer #(.select(3), .width(8)) multiplexer_1 (
    .in0(ULA_in), .in1(NOT_ULA_in), .in2(bit_extender_1_out), .in3(bit_extender_2_out),
    .in4(bit_extender_3_out), .in5(ULA_in), .in6(ULA_in), .in7(ULA_in), .out(RESPONSE_SELECTED),
    .sel(Select_response));
endmodule

module Decodofication (
  input  [2:0] BIN_in,
  output [2:0] BIN_out
);

  wire decoder_1_out0, decoder_1_out1, decoder_1_out2, decoder_1_out3, priority_encoder_1_gs;
  wire [2:0] bit_extender_1_out, priority_encoder_1_out;

  Decoder #(.enable("false"), .select(3)) decoder_1 (
    .out0(decoder_1_out0), .out1(decoder_1_out1), .out2(decoder_1_out2), .out3(decoder_1_out3), .sel(BIN_in));  // open: out4, out5, out6, out7
  Priority_Encoder priority_encoder_1 (
    .in3(decoder_1_out0), .in4(decoder_1_out1), .in5(decoder_1_out2), .in6(decoder_1_out3),
    .out(priority_encoder_1_out), .gs(priority_encoder_1_gs));  // open: in0, in1, in2, in7, en_in, en_out
  assign BIN_out = priority_encoder_1_out & bit_extender_1_out;  // AND_Gate and_1, 3 bits wide
  assign bit_extender_1_out = {{2{priority_encoder_1_gs}}, priority_encoder_1_gs};  // Bit_Extender bit_extender_1
endmodule
